# Fritzing sketch WiFiModule - Display (saved by Fritzing 0.9.3b)
breadboards: 1

parts:
  LCD1 = LCD screen [part_number="JDH 162A"]
  Componente1 = Arduino Mega ADK (Rev3)
  R2 = Trimmer Potentiometer [maximum_resistance=10kΩ package=THT]
  R1 = Trimmer Potentiometer [maximum_resistance=10kΩ package=THT]

nets:
  VSS: LCD1.VSS, LCD1.R/W, LCD1.LED-, Componente1.GND, R2.leg1, R1.leg1
  VDD: LCD1.VDD, Componente1.5V, R2.leg2, R1.leg2
  N1: LCD1.V0, R1.wiper
  N2: LCD1.RS, Componente1.D12_PWM
  N3: LCD1.E, Componente1.D11_PWM
  N4: LCD1.DB4, Componente1.D5_PWM
  N5: LCD1.DB5, Componente1.D4_PWM
  N6: LCD1.DB6, Componente1.D3_PWM
  N7: LCD1.DB7, Componente1.D2_PWM
  N8: LCD1.LED+, R2.wiper
