# Fritzing sketch WiFiModule - ESP8266 (saved by Fritzing 0.9.3b)
breadboards: 1
perfboards: 1

parts:
  Componente1 = Arduino Mega ADK (Rev3)  # not connected
  J2 = female pin header, 4 pins [form="♀ (female)"]
  U1 = ESP8266 WiFi Module [part_number=ESP8266]

nets:
  N1: J2.pin2, U1.GPIO_4

notes:
  http://www.dx.com/pt/p/400559
  GND / VCC / TX / RX
